// Logisim project 1F1.circ as structural Verilog: 1 circuit, main circuit main
module main (
  input  B,
  input  A,
  input  C,
  output F1
);

  wire AND_star_p3, OR_plus_p3, OR_plus_p5, OR_plus_p6;

  // _7432 OR_plus: pin names not known; wires that end beside it: B, A, OR_plus_p3, C, OR_plus_p5, OR_plus_p6, 1'b0, 1'b1
  // _7404 7404_1: pin names not known; wires that end beside it: A, OR_plus_p5, 1'b0, 1'b1
  // _7408 AND_star: pin names not known; wires that end beside it: OR_plus_p3, C, AND_star_p3, AND_star_p3, OR_plus_p6, F1, 1'b0, 1'b1

  // Notes on the sheet:
  //   GND
  //   GND
  //   NOT
  //   VCC
  //   GND
endmodule
