// Logisim project 1F2.circ as structural Verilog: 1 circuit, main circuit main
module main (
  input  A,
  input  B,
  input  C,
  output F2
);

  wire main_1_f1;

  _1F1_main main_1 (.B(B), .A(A), .C(C), .F1(main_1_f1));
  // _7432 7432_1: pin names not known; wires that end beside it: main_1_f1, A, F2, 1'b0, 1'b1
endmodule
