// Logisim project Circuit 1.circ as structural Verilog: 1 circuit, main circuit main
module main (
  input  S1,
  input  S2,
  output out_3
);

  // _7408 AND_IC: pin names not known; wires that end beside it: S1, S2, out_3, 1'b0, 1'b1
endmodule
