// Logisim project F1.circ as structural Verilog: 1 circuit, main circuit main
module main (
  input  in_1,
  input  in_2,
  input  in_3,
  output out_4
);

  wire n7404_1_p2, n7404_1_p4, n7408_1_p3, n7408_1_p6, n7408_1_p11, n7432_1_p3;

  // _7404 7404_1: pin names not known; wires that end beside it: in_1, n7404_1_p2, in_2, n7404_1_p4, 1'b0, 1'b1
  // _7408 7408_1: pin names not known; wires that end beside it: in_1, in_2, n7408_1_p3, n7404_1_p2, n7404_1_p4, n7408_1_p6, 1'b0, 1'b1, n7404_1_p4, in_3, n7408_1_p11
  // _7432 7432_1: pin names not known; wires that end beside it: n7408_1_p3, n7408_1_p6, n7432_1_p3, n7432_1_p3, n7408_1_p11, out_4, 1'b0, 1'b1
endmodule
