// Logisim project F2.circ as structural Verilog: 1 circuit, main circuit main
module main (
  input  in_1,
  input  in_2,
  input  in_3,
  output out_4
);

  wire main_1_out_4;

  F1_main main_1 (.in_1(in_1), .in_2(in_2), .in_3(in_3), .out_4(main_1_out_4));
  // _7404 7404_1: pin names not known; wires that end beside it: main_1_out_4, out_4, 1'b0, 1'b1
endmodule
