// Logisim project Finalo log.circ as structural Verilog
module Addition (
  input  X0,
  input  Y0,
  input  SY,
  input  SX,
  input  X1,
  input  Y1,
  output S0,
  output S1,
  output S2,
  output Sign
);

  wire comparator_1_out_5, n7408_2_p2, n7486_1_p3, n7486_1_p6, n7486_1_p10, n7486_1_p11, n7486_1_p13,
       n7486_1_p14, n7486_2_p3, n7486_2_p6, n7486_2_p11, n7486_2_p12, n7486_2_p13, n7486_3_p3, n7486_3_p6;

  comparator comparator_1 (.X0(X0), .X1(X1), .Y0(Y0), .Y1(Y1), .out_5(comparator_1_out_5));
  // _7486 7486_1: pin names not known; wires that end beside it: SY, SX, n7486_1_p3, comparator_1_out_5, 1'b1, n7486_1_p6, 1'b0, 1'b1, X0, n7486_1_p10, n7486_1_p11, Y0, n7486_1_p13, n7486_1_p14
  // _7486 7486_2: pin names not known; wires that end beside it: SY, SX, n7486_2_p3, n7486_1_p10, X1, n7486_2_p6, 1'b0, 1'b1, 1'b0, Y1, n7486_2_p11, n7486_2_p12, n7486_2_p13, Sign
  // _7408 7408_1: pin names not known; wires that end beside it: n7486_1_p3, n7486_1_p6, n7486_1_p10, n7486_1_p3, comparator_1_out_5, n7486_1_p13, 1'b0, 1'b1, SX, comparator_1_out_5, n7486_2_p12, n7486_1_p6, SY, n7486_2_p13
  // _7486 7486_3: pin names not known; wires that end beside it: SX, SY, n7486_3_p3, n7486_3_p3, 1'b1, n7486_3_p6
  // _7408 7408_2: pin names not known; wires that end beside it: n7486_3_p6, n7408_2_p2, S2
  // _7483 7483_1: pin names not known; wires that end beside it: 1'b0, n7408_2_p2, 1'b0, 1'b0, 1'b1, S1, n7486_2_p11, n7486_2_p6, 1'b0, n7486_2_p3, 1'b0, n7486_1_p14, n7486_1_p11, S0
endmodule

module Comparator (
  input  X0,
  input  X1,
  input  Y0,
  input  Y1,
  output out_5
);

  wire n7408_1_p3, n7408_1_p6, n7408_1_p11, n7486_1_p3, n7486_1_p6, n7486_1_p11, n7486_1_p14;

  // _7486 7486_1: pin names not known; wires that end beside it: X1, Y1, n7486_1_p3, n7486_1_p3, 1'b1, n7486_1_p6, 1'b0, 1'b1, Y0, 1'b1, n7486_1_p11, Y1, 1'b1, n7486_1_p14
  // _7408 7408_1: pin names not known; wires that end beside it: X0, n7486_1_p11, n7408_1_p3, n7408_1_p3, n7486_1_p6, n7408_1_p6, 1'b0, 1'b1, n7486_1_p14, X1, n7408_1_p11
  // _7432 7432_1: pin names not known; wires that end beside it: n7408_1_p11, n7408_1_p6, out_5, out_5
endmodule

module Remainder (
  input  X0,
  input  X1,
  input  SIGNX,
  input  Y0,
  input  Y1,
  input  SIGN_Y,
  output s0,
  output s1,
  output dvide_zero,
  output sign
);

  wire n7408_1_p3, n7408_1_p6, n7408_2_p3, n7408_2_p6, n7408_2_p11, n7408_2_p14, not_1_out, not_2_out,
       not_3_out, not_4_out, not_5_out;

  not not_1 (not_1_out, X1);
  not not_2 (not_2_out, Y0);
  not not_3 (not_3_out, Y1);
  not not_4 (not_4_out, Y0);
  not not_5 (not_5_out, X0);
  // _7408 7408_1: pin names not known; wires that end beside it: Y0, not_5_out, n7408_1_p3, X1, Y1, n7408_1_p6, 1'b0, 1'b1, n7408_1_p6, n7408_1_p3, s1, not_2_out, not_3_out, dvide_zero
  // _7408 7408_2: pin names not known; wires that end beside it: Y1, X0, n7408_2_p3, n7408_2_p3, not_4_out, n7408_2_p6, 1'b0, 1'b1, X0, not_1_out, n7408_2_p11, n7408_2_p11, Y1, n7408_2_p14
  // _7432 7432_1: pin names not known; wires that end beside it: n7408_2_p14, n7408_2_p6, s0, 1'b0, 1'b1

  assign sign = SIGNX;
endmodule

module Multiplyer (
  input  X0,
  input  X1,
  input  SIGN_X,
  input  y0,
  input  Y1,
  input  SIgn_y,
  output out_7,
  output out_8,
  output out_9,
  output out_10,
  output out_11
);

  wire n7408_1_p6, n7408_1_p11, n7408_1_p14;

  // _7408 7408_1: pin names not known; wires that end beside it: X0, y0, out_7, X0, Y1, n7408_1_p6, 1'b0, 1'b1, X1, y0, n7408_1_p11, Y1, X1, n7408_1_p14
  // _7486 7486_1: pin names not known; wires that end beside it: SIGN_X, SIgn_y, out_11, 1'b0, 1'b1
  // _7483 7483_1: pin names not known; wires that end beside it: 1'b0, out_10, 1'b0, 1'b0, 1'b1, out_9, 1'b0, n7408_1_p14, 1'b0, 1'b0, 1'b0, n7408_1_p11, n7408_1_p6, out_8

  // Notes on the sheet:
  //   2
endmodule
