// Logisim project Project_Logic (1).circ as structural Verilog: 7 circuits, main circuit main
module main (
  input  X0,
  input  Y0,
  input  Sy,
  input  Sx,
  input  X1,
  input  Y1,
  output S0,
  output S1,
  output out_9,
  output out_10
);

  wire and_1_out, and_2_out, and_3_out, and_4_out, comparator_1_out_5, full_adder_1_cout, full_adder_2_cout,
       not_1_out, xnor_1_out, xor_1_out, xor_2_out, xor_3_out, xor_4_out, xor_5_out, xor_6_out;

  comparator comparator_1 (.X0(X0), .X1(X1), .Y0(Y0), .Y1(Y1), .out_5(comparator_1_out_5));
  xor xor_1 (xor_1_out, Sy, Sx);
  and and_1 (and_1_out, xor_1_out, comparator_1_out_5);
  not not_1 (not_1_out, comparator_1_out_5);
  and and_2 (and_2_out, xor_1_out, not_1_out);
  xor xor_2 (xor_2_out, X0, and_2_out);
  xor xor_3 (xor_3_out, and_2_out, X1);
  xor xor_4 (xor_4_out, and_1_out, Y1);
  // _7486 7486_1: pin names not known
  xor xor_5 (xor_5_out, Y0, and_1_out);
  xor xor_6 (xor_6_out, Sy, Sx);
  full_adder full_adder_1 (.x(xor_2_out), .y(xor_5_out), .cin(xor_6_out), .sum(S0), .cout(full_adder_1_cout));
  full_adder full_adder_2 (.x(xor_3_out), .y(xor_4_out), .cin(full_adder_1_cout), .sum(S1), .cout(full_adder_2_cout));
  xnor xnor_1 (xnor_1_out, Sx, Sy);
  and and_3 (and_3_out, comparator_1_out_5, Sx);
  and and_4 (and_4_out, not_1_out, Sy);
  and and_5 (out_9, xnor_1_out, full_adder_2_cout);
  xor xor_7 (out_10, and_3_out, and_4_out);
endmodule

// FA
module full_adder (
  input  x,
  input  y,
  input  cin,
  output sum,
  output cout
);

  wire and_1_out, and_2_out, and_3_out, xor_1_out;

  xor xor_1 (xor_1_out, x, y);
  and and_1 (and_1_out, x, y);
  and and_2 (and_2_out, x, cin);
  and and_3 (and_3_out, y, cin);
  xor xor_2 (sum, xor_1_out, cin);
  or or_1 (cout, and_1_out, and_2_out, and_3_out);
endmodule

module comparator (
  input  X0,
  input  X1,
  input  Y0,
  input  Y1,
  output out_5
);

  wire n7408_1_p3, n7408_1_p6, n7408_1_p11, n7486_1_p3, n7486_1_p6, n7486_1_p11, n7486_1_p14;

  // _7486 7486_1: pin names not known; wires that end beside it: X1, Y1, n7486_1_p3, n7486_1_p3, 1'b1, n7486_1_p6, 1'b0, 1'b1, Y0, 1'b1, n7486_1_p11, Y1, 1'b1, n7486_1_p14
  // _7408 7408_1: pin names not known; wires that end beside it: X0, n7486_1_p11, n7408_1_p3, n7408_1_p3, n7486_1_p6, n7408_1_p6, 1'b0, 1'b1, n7486_1_p14, X1, n7408_1_p11
  // _7432 7432_1: pin names not known; wires that end beside it: n7408_1_p11, n7408_1_p6, out_5, out_5
endmodule

module rem (
  input  X0,
  input  X1,
  input  SIGNX,
  input  Y0,
  input  Y1,
  input  SIGN_Y,
  output Ro,
  output R1,
  output Flag_zero,
  output sign
);

  wire and_2_out, and_3_out, not_1_out, not_2_out, not_3_out, not_4_out, not_5_out;

  not not_1 (not_1_out, X1);
  not not_2 (not_2_out, Y0);
  not not_3 (not_3_out, Y1);
  not not_4 (not_4_out, Y0);
  not not_5 (not_5_out, X0);
  and and_1 (Flag_zero, not_2_out, not_3_out);
  and and_2 (and_2_out, X0, Y1, not_4_out);
  and and_3 (and_3_out, X0, not_1_out, Y1);
  and and_4 (R1, Y0, not_5_out, X1, Y1);
  or or_1 (Ro, and_2_out, and_3_out);

  assign sign = SIGNX;
endmodule

module \new  (
  input  B,
  input  A,
  input  X0,
  input  X1,
  input  SIGNX,
  input  Y0,
  input  Y1,
  input  SIGN_Y,
  output _1_bit,
  output _2_bit,
  output _3_bit,
  output bit_4,
  output sign_flag,
  output answer__0_flag,
  output out_15
);

  wire main_1_out_7, main_1_out_8, main_1_out_9, main_1_out_10, main_1_out_11, main_2_s0, main_2_s1,
       main_2_s2, main_2_sign, main_3_s0, main_3_s1, main_3_s2, main_3_sign, main_4_dvide_zero, main_4_s0,
       main_4_s1, main_4_sign, n7408_1_p3, n7408_1_p7, n7408_1_p8, n7408_2_p3, n7408_2_p9, n7432_1_p3,
       n7432_1_p6, n7448_1_p10, n7448_1_p11, n7448_1_p12, n7448_1_p13, n7448_1_p14, n7448_1_p15, n7448_1_p16,
       n7448_2_p10, n7448_2_p11, n7448_2_p12, n7448_2_p13, n7448_2_p14, n7448_2_p15, n7448_2_p16,
       n74153_2_p16, not_1_out, not_2_out, not_4_out;

  not not_1 (not_1_out, SIGN_Y);
  half_adder_main main_1 (
    .X0(X0), .X1(X1), .SIGN_X(SIGNX), .y0(Y0), .Y1(Y1), .SIgn_y(SIGN_Y), .out_7(main_1_out_7),
    .out_8(main_1_out_8), .out_9(main_1_out_9), .out_10(main_1_out_10), .out_11(main_1_out_11));
  full_adder__4__main main_2 (
    .X0(X0), .Y0(Y0), .SY(not_1_out), .SX(SIGNX), .X1(X1), .Y1(Y1), .S0(main_2_s0), .S1(main_2_s1),
    .S2(main_2_s2), .Sign(main_2_sign));
  full_adder__4__main main_3 (
    .X0(X0), .Y0(Y0), .SY(SIGN_Y), .SX(SIGNX), .X1(X1), .Y1(Y1), .S0(main_3_s0), .S1(main_3_s1),
    .S2(main_3_s2), .Sign(main_3_sign));
  ZICO_main main_4 (
    .X0(X0), .X1(X1), .SIGNX(SIGNX), .Y0(Y0), .Y1(Y1), .SIGN_Y(SIGN_Y), .s0(main_4_s0), .s1(main_4_s1),
    .dvide_zero(main_4_dvide_zero), .sign(main_4_sign));
  // _7408 7408_1: pin names not known; wires that end beside it: A, B, n7408_1_p3, n7408_1_p3, main_4_dvide_zero, out_15, n7408_1_p7, n7408_1_p8, answer__0_flag
  // _74153 74153_1: pin names not known; wires that end beside it: 1'b0, A, main_4_s0, main_1_out_7, main_2_s0, main_3_s0, _1_bit, 1'b0, 1'b1, 1'b0, B, main_4_s1, main_1_out_8, main_2_s1, main_3_s1, _2_bit
  // _74153 74153_2: pin names not known; wires that end beside it: 1'b0, A, 1'b0, main_1_out_9, main_2_s2, main_3_s2, _3_bit, 1'b0, 1'b1, 1'b0, B, main_4_sign, main_1_out_11, main_2_sign, main_3_sign, n74153_2_p16
  not not_2 (not_2_out, out_15);
  not not_3 (n7408_1_p7, n7432_1_p3);
  // _7448 7448_1: pin names not known; wires that end beside it: _2_bit, _3_bit, 1'b1, 1'b1, not_2_out, bit_4, _1_bit, 1'b0, 1'b1, n7448_1_p10, n7448_1_p11, n7448_1_p12, n7448_1_p13, n7448_1_p14, n7448_1_p15, n7448_1_p16
  not not_4 (not_4_out, B);
  not not_5 (n7408_1_p8, n7432_1_p6);
  // _7408 7408_2: pin names not known; wires that end beside it: not_4_out, A, n7408_2_p3, n7408_2_p3, main_1_out_10, bit_4, 1'b1, n74153_2_p16, n7408_2_p9, sign_flag
  _7_Segment_Display u_7_segment_display_1 (
    .g(n7448_1_p11), .f(n7448_1_p10), .a(n7448_1_p12), .b(n7448_1_p13), .e(n7448_1_p16), .d(n7448_1_p15),
    .c(n7448_1_p14));  // open: dp
  // _7432 7432_1: pin names not known; wires that end beside it: _1_bit, _2_bit, n7432_1_p3, bit_4, _3_bit, n7432_1_p6, 1'b0, 1'b1, n7432_1_p6, n7432_1_p3, n7408_2_p9
  // _7448 7448_2: pin names not known; wires that end beside it: 1'b0, 1'b0, 1'b1, 1'b1, not_2_out, 1'b0, sign_flag, 1'b0, 1'b1, n7448_2_p10, n7448_2_p11, n7448_2_p12, n7448_2_p13, n7448_2_p14, n7448_2_p15, n7448_2_p16
  _7_Segment_Display u_7_segment_display_2 (
    .g(n7448_2_p11), .f(n7448_2_p10), .a(n7448_2_p12), .b(n7448_2_p13), .e(n7448_2_p16), .d(n7448_2_p15),
    .c(n7448_2_p14));  // open: dp

  // Notes on the sheet:
  //   Rem
  //   Multiplayer
  //   Subtractor
  //   Adder
  //   Divided by zero flag
  //   NO.
  //   Sign
endmodule

module Multiplyer (
  input  X0,
  input  X1,
  input  Sx,
  input  Y1,
  input  Y2,
  input  Sy,
  output m0,
  output m1,
  output m2,
  output m3,
  output sign
);

  wire and_2_out, and_3_out, and_4_out, ha_1_carry;

  and and_1 (m0, X0, Y1);
  and and_2 (and_2_out, X0, Y2);
  and and_3 (and_3_out, Y1, X1);
  xor xor_1 (sign, Sx, Sy);
  HA ha_1 (.in_1(and_2_out), .in_2(and_3_out), .sum(m1), .carry(ha_1_carry));
  and and_4 (and_4_out, X1, Y2);
  HA ha_2 (.in_1(ha_1_carry), .in_2(and_4_out), .sum(m2), .carry(m3));
endmodule

module HA (
  input  in_1,
  input  in_2,
  output sum,
  output carry
);

  xor xor_1 (sum, in_1, in_2);
  and and_1 (carry, in_2, in_1);
endmodule
