// Logisim project ZICO.circ as structural Verilog: 2 circuits, main circuit main
module main (
  input  X0,
  input  X1,
  input  SIGNX,
  input  Y0,
  input  Y1,
  input  SIGN_Y,
  output s0,
  output s1,
  output dvide_zero,
  output sign
);

  wire n7408_1_p3, n7408_1_p6, n7408_2_p3, n7408_2_p6, n7408_2_p11, n7408_2_p14, not_1_out, not_2_out,
       not_3_out, not_4_out, not_5_out;

  not not_1 (not_1_out, X1);
  not not_2 (not_2_out, Y0);
  not not_3 (not_3_out, Y1);
  not not_4 (not_4_out, Y0);
  not not_5 (not_5_out, X0);
  // _7408 7408_1: pin names not known; wires that end beside it: Y0, not_5_out, n7408_1_p3, X1, Y1, n7408_1_p6, 1'b0, 1'b1, n7408_1_p6, n7408_1_p3, s1, not_2_out, not_3_out, dvide_zero
  // _7408 7408_2: pin names not known; wires that end beside it: Y1, X0, n7408_2_p3, n7408_2_p3, not_4_out, n7408_2_p6, 1'b0, 1'b1, X0, not_1_out, n7408_2_p11, n7408_2_p11, Y1, n7408_2_p14
  // _7432 7432_1: pin names not known; wires that end beside it: n7408_2_p14, n7408_2_p6, s0, 1'b0, 1'b1

  assign sign = SIGNX;
endmodule

module HA (
  input  in_1,
  input  in_2,
  output SUM,
  output CARRY
);

  xor xor_1 (SUM, in_1, in_2);
  and and_1 (CARRY, in_1, in_2);
endmodule
