// Logisim project full-adder (4).circ as structural Verilog
module main (
  input  X0,
  input  Y0,
  input  SY,
  input  SX,
  input  X1,
  input  Y1,
  output S0,
  output S1,
  output S2,
  output Sign
);

  wire comparator_1_out_5, n7408_2_p2, n7486_1_p3, n7486_1_p6, n7486_1_p10, n7486_1_p11, n7486_1_p13,
       n7486_1_p14, n7486_2_p3, n7486_2_p6, n7486_2_p11, n7486_2_p12, n7486_2_p13, n7486_3_p3, n7486_3_p6;

  comparator comparator_1 (.X0(X0), .X1(X1), .Y0(Y0), .Y1(Y1), .out_5(comparator_1_out_5));
  // _7486 7486_1: pin names not known; wires that end beside it: SY, SX, n7486_1_p3, comparator_1_out_5, 1'b1, n7486_1_p6, 1'b0, 1'b1, X0, n7486_1_p10, n7486_1_p11, Y0, n7486_1_p13, n7486_1_p14
  // _7486 7486_2: pin names not known; wires that end beside it: SY, SX, n7486_2_p3, n7486_1_p10, X1, n7486_2_p6, 1'b0, 1'b1, 1'b0, Y1, n7486_2_p11, n7486_2_p12, n7486_2_p13, Sign
  // _7408 7408_1: pin names not known; wires that end beside it: n7486_1_p3, n7486_1_p6, n7486_1_p10, n7486_1_p3, comparator_1_out_5, n7486_1_p13, 1'b0, 1'b1, SX, comparator_1_out_5, n7486_2_p12, n7486_1_p6, SY, n7486_2_p13
  // _7486 7486_3: pin names not known; wires that end beside it: SX, SY, n7486_3_p3, n7486_3_p3, 1'b1, n7486_3_p6
  // _7408 7408_2: pin names not known; wires that end beside it: n7486_3_p6, n7408_2_p2, S2
  // _7483 7483_1: pin names not known; wires that end beside it: 1'b0, n7408_2_p2, 1'b0, 1'b0, 1'b1, S1, n7486_2_p11, n7486_2_p6, 1'b0, n7486_2_p3, 1'b0, n7486_1_p14, n7486_1_p11, S0
endmodule

// FA
module full_adder (
  input  x,
  input  y,
  input  cin,
  output sum,
  output cout
);

  wire and_1_out, and_2_out, and_3_out, xor_1_out;

  xor xor_1 (xor_1_out, x, y);
  and and_1 (and_1_out, x, y);
  and and_2 (and_2_out, x, cin);
  and and_3 (and_3_out, y, cin);
  xor xor_2 (sum, xor_1_out, cin);
  or or_1 (cout, and_1_out, and_2_out, and_3_out);
  main main_1 ();  // open: X0, Y0, SY, SX, X1, Y1, S0, S1, S2, Sign
endmodule

module comparator (
  input  X0,
  input  X1,
  input  Y0,
  input  Y1,
  output out_5
);

  wire n7408_1_p3, n7408_1_p6, n7408_1_p11, n7486_1_p3, n7486_1_p6, n7486_1_p11, n7486_1_p14;

  // _7486 7486_1: pin names not known; wires that end beside it: X1, Y1, n7486_1_p3, n7486_1_p3, 1'b1, n7486_1_p6, 1'b0, 1'b1, Y0, 1'b1, n7486_1_p11, Y1, 1'b1, n7486_1_p14
  // _7408 7408_1: pin names not known; wires that end beside it: X0, n7486_1_p11, n7408_1_p3, n7408_1_p3, n7486_1_p6, n7408_1_p6, 1'b0, 1'b1, n7486_1_p14, X1, n7408_1_p11
  // _7432 7432_1: pin names not known; wires that end beside it: n7408_1_p11, n7408_1_p6, out_5, out_5
endmodule

module rem (
  input  X0,
  input  X1,
  input  SIGNX,
  input  Y0,
  input  Y1,
  input  SIGN_Y,
  output R0,
  output R1,
  output FLAG_ZERO,
  output out_10
);

  wire and_2_out, and_3_out, not_1_out, not_2_out, not_3_out, not_4_out, not_5_out;

  not not_1 (not_1_out, X1);
  not not_2 (not_2_out, Y0);
  not not_3 (not_3_out, Y1);
  not not_4 (not_4_out, Y0);
  not not_5 (not_5_out, X0);
  and and_1 (FLAG_ZERO, not_2_out, not_3_out);
  and and_2 (and_2_out, X0, Y1, not_4_out);
  and and_3 (and_3_out, X0, not_1_out, Y1);
  and and_4 (R1, Y0, not_5_out, X1, Y1);
  or or_1 (R0, and_2_out, and_3_out);

  assign out_10 = SIGNX;
endmodule

module \new  (
  input  in_1,
  input  in_2,
  input  in_3,
  input  in_4,
  input  in_5,
  input  in_6,
  input  in_7,
  input  in_8,
  input  X0,
  input  in_10,
  input  in_11,
  input  X1,
  input  SIGNX,
  input  Y0,
  input  Y1,
  input  SIGN_Y,
  output output_1,
  output output_2
);

  Multiplexer #(.select(2)) multiplexer_1 ();  // open: in0, in1, in2, in3, out, sel, en
  Multiplexer #(.select(2)) multiplexer_2 ();  // open: in0, in1, in2, in3, out, sel, en
  Multiplexer #(.select(2)) multiplexer_3 ();  // open: in0, in1, in2, in3, out, sel, en
  // _74153 74153_1: pin names not known; wires that end beside it: 1'b0, in_1, in_3, in_8, in_10, in_11, output_1, 1'b0, 1'b1, 1'b0, in_2, in_4, in_6, in_7, output_2, in_5
  // _7448 7448_1: pin names not known

  // Notes on the sheet:
  //   Mode of operations
endmodule
