// Logisim project half-adder.circ as structural Verilog: 2 circuits, main circuit Half-Adder
module Half_Adder (
  input  in_1,
  input  in_2,
  output sum,
  output carry
);

  xor xor_1 (sum, in_1, in_2);
  and and_1 (carry, in_2, in_1);
endmodule

module main (
  input  X0,
  input  X1,
  input  SIGN_X,
  input  y0,
  input  Y1,
  input  SIgn_y,
  output out_7,
  output out_8,
  output out_9,
  output out_10,
  output out_11
);

  wire n7408_1_p6, n7408_1_p11, n7408_1_p14;

  // _7408 7408_1: pin names not known; wires that end beside it: X0, y0, out_7, X0, Y1, n7408_1_p6, 1'b0, 1'b1, X1, y0, n7408_1_p11, Y1, X1, n7408_1_p14
  // _7486 7486_1: pin names not known; wires that end beside it: SIGN_X, SIgn_y, out_11, 1'b0, 1'b1, 1'b0
  // _7483 7483_1: pin names not known; wires that end beside it: 1'b0, out_10, 1'b0, 1'b0, 1'b1, out_9, 1'b0, n7408_1_p14, 1'b0, 1'b0, 1'b0, n7408_1_p11, n7408_1_p6, out_8

  // Notes on the sheet:
  //   1
  //   2
  //   3
endmodule
